// Logisim project MyFile.circ as structural Verilog: 1 circuit, main circuit main
module main (
  input  in_1
);

  wire button_1_out, button_2_out, clock_1_out, not_1_out;
  wire [3:0] multiplexer_1_out;
  wire [7:0] ram_1_dout, random_1_out;
  wire [15:0] counter_1_q;

  Clock clock_1 (.out(clock_1_out));
  Button button_1 (.out(button_1_out));
  Counter #(.max('hffff), .width(16)) counter_1 (
    .clr(button_1_out), .clk(clock_1_out), .Q(counter_1_q));  // open: load, up, count, D, carry
  Random random_1 (.clr(1'b0), .next(1'b1), .clk(clock_1_out), .out(random_1_out));
  not not_1 (not_1_out, in_1);
  Button button_2 (.out(button_2_out));
  RAM #(.addrWidth(16), .clearpin("true")) ram_1 (
    .addr(counter_1_q), .we(not_1_out), .oe(not_1_out), .clk(clock_1_out), .din(random_1_out),
    .dout(ram_1_dout), .clr(button_2_out));
  Hex_Digit_Display #(.decimalPoint("false")) hex_digit_display_1 (.value(multiplexer_1_out));
  Multiplexer #(.disabled("Z"), .enable("true"), .width(4)) multiplexer_1 (
    .in0(4'b1110), .in1(4'b1010), .out(multiplexer_1_out), .sel(ram_1_dout[0]), .en(1'b1));
endmodule
