// Logisim project Nitin_Johnoson.circ as structural Verilog: 1 circuit, main circuit main
module main (
  output out_1,
  output out_2,
  output out_3,
  output out_4,
  output out_5,
  output out_6,
  output out_7,
  output out_8
);

  wire button_1_out, button_2_out, clock_1_out, clock_2_out, not_1_out;

  Clock clock_1 (.out(clock_1_out));
  Button button_1 (.out(button_1_out));
  D_Flip_Flop d_ff_1 (.D(not_1_out), .clk(clock_1_out), .Q(out_1), .reset(button_1_out));  // open: Qn, preset
  D_Flip_Flop d_ff_2 (.D(out_1), .clk(clock_1_out), .Q(out_2), .reset(button_1_out));  // open: Qn, preset
  D_Flip_Flop d_ff_3 (.D(out_2), .clk(clock_1_out), .Q(out_3), .reset(button_1_out));  // open: Qn, preset
  D_Flip_Flop d_ff_4 (.D(out_3), .clk(clock_1_out), .Q(out_4), .reset(button_1_out));  // open: Qn, preset
  Clock clock_2 (.out(clock_2_out));
  Button button_2 (.out(button_2_out));
  not not_1 (not_1_out, out_4);
  D_Flip_Flop d_ff_5 (.D(out_8), .clk(clock_2_out), .Q(out_5), .reset(button_2_out));  // open: Qn, preset
  D_Flip_Flop d_ff_6 (.D(out_5), .clk(clock_2_out), .Q(out_6), .reset(button_2_out));  // open: Qn, preset
  D_Flip_Flop d_ff_7 (.D(out_6), .clk(clock_2_out), .Q(out_7), .reset(button_2_out));  // open: Qn, preset
  D_Flip_Flop d_ff_8 (.D(out_7), .clk(clock_2_out), .Q(out_8), .reset(button_2_out));  // open: Qn, preset
endmodule
