// Logisim project PB3.circ as structural Verilog: 1 circuit, main circuit main
module main (
  input  Read_Write_Pin
);

  wire clock_1_out, not_1_out, Reset_Counter_out, Reset_RAM_out;
  wire [3:0] multiplexer_1_out;
  wire [7:0] ram_1_data, random_1_out;
  wire [15:0] counter_1_q;

  Clock clock_1 (.out(clock_1_out));
  Counter #(.width(16), .max('hffff)) counter_1 (
    .count(1'b1), .Q(counter_1_q), .clk(clock_1_out), .clr(Reset_Counter_out));  // open: load, D, carry
  Button Reset_Counter (.out(Reset_Counter_out));
  Random random_1 (.clk(clock_1_out), .next(1'b1), .out(random_1_out), .clr(1'b0));
  not not_1 (not_1_out, Read_Write_Pin);
  RAM #(.addrWidth(16), .bus("separate")) ram_1 (
    .addr(counter_1_q), .din(random_1_out), .data(ram_1_data), .str(not_1_out), .clk(clock_1_out),
    .ld(Read_Write_Pin), .clr(Reset_RAM_out));  // open: sel
  Button Reset_RAM (.out(Reset_RAM_out));
  Multiplexer #(.width(4)) multiplexer_1 (
    .in0(4'b1110), .in1(4'b1010), .out(multiplexer_1_out), .sel(ram_1_data[0]), .en(1'b1));
  Hex_Digit_Display hex_digit_display_1 (.value(multiplexer_1_out));  // open: dp
endmodule
